// Logisim project 64bitCPU.circ as structural Verilog: 18 circuits, main circuit FullAdder64
module FullAdder64 (
  input  [63:0] In,
  input  [63:0] A,
  input  [63:0] B,
  output [63:0] Result,
  output [63:0] Out
);

  wire [63:0] and_1_out, AND_2_out, XOR_out;

  assign and_1_out = A & B;  // AND_Gate and_1, 64 bits wide
  assign XOR_out = A ^ B;  // XOR_Gate XOR, 64 bits wide
  assign Out = and_1_out ^ AND_2_out;  // XOR_Gate OR, 64 bits wide
  assign AND_2_out = In & XOR_out;  // AND_Gate AND_2, 64 bits wide
  assign Result = In ^ XOR_out;  // XOR_Gate xor_2, 64 bits wide
endmodule

// ADD
module Adder64 (
  input  [63:0] Control,
  input  [63:0] A,
  input  [63:0] B,
  output [63:0] Result,
  output [63:0] CarryOut,
  output [63:0] Overflow
);

  wire [63:0] and_1_out, AND_2_out, not_1_out, not_2_out, not_3_out;

  assign not_1_out = ~B;  // NOT_Gate not_1, 64 bits wide
  assign not_2_out = ~A;  // NOT_Gate not_2, 64 bits wide
  FullAdder64 fulladder64_1 (.A(A), .B(B), .In(Control), .Out(CarryOut), .Result(Result));
  assign and_1_out = Result & not_2_out & not_1_out;  // AND_Gate and_1, 64 bits wide
  assign not_3_out = ~Result;  // NOT_Gate not_3, 64 bits wide
  assign AND_2_out = not_3_out & A & B;  // AND_Gate AND_2, 64 bits wide
  assign Overflow = and_1_out | AND_2_out;  // OR_Gate or_1, 64 bits wide
endmodule

// AND
module AND64 (
  input  [63:0] A,
  input  [63:0] B,
  output [63:0] Result
);

  assign Result = A & B;  // AND_Gate and_1, 64 bits wide
endmodule

// OR
module OR64 (
  input  [63:0] A,
  input  [63:0] B,
  output [63:0] Result
);

  assign Result = A | B;  // OR_Gate or_1, 64 bits wide
endmodule

// ALU
module ALU64 (
  input  [63:0] B,
  input  [3:0] OpCodeIn,
  input  [63:0] A,
  output [63:0] Carryout,
  output [63:0] Overflow,
  output [63:0] ALUResult,
  output GT,
  output EQ,
  output LT,
  output [31:0] ZERO,
  output [31:0] Negative
);

  wire [31:0] clear64_1_result, OR_out;
  wire [63:0] adder64_1_result, and64_1_result, decrementer64_1_result, incrementer64_1_result,
       leftshift64_1_result, nand64_1_result, nor64_1_result, not64_1_result, or64_1_result,
       rightshift64_1_result, xnor64_1_result, xor64_1_p3;

  Adder64 adder64_1 (
    .A(A), .B(B), .Result(adder64_1_result), .CarryOut(Carryout), .Overflow(Overflow));  // open: Control
  Incrementer64 incrementer64_1 (.A(A), .Result(incrementer64_1_result));  // open: Control, CarryOut, Overflow
  Decrementer64 decrementer64_1 (.A(A), .Result(decrementer64_1_result));  // open: Control, CarryOut, Overflow
  Comparator64 comparator64_1 (.A(A), .B(B), .GT(GT), .EQ(EQ), .LT(LT));
  NOT64 not64_1 (.Result(not64_1_result));  // open: A
  AND64 and64_1 (.A(A), .Result(and64_1_result));  // open: B
  OR64 or64_1 (.A(A), .Result(or64_1_result));  // open: B
  LeftShift64 leftshift64_1 (.A(A), .Result(leftshift64_1_result));
  RightShift64 rightshift64_1 (.A(A), .Result(rightshift64_1_result));
  NAND64 nand64_1 (.A(A), .Result(nand64_1_result));  // open: B
  NOR64 nor64_1 (.A(A), .Result(nor64_1_result));  // open: B
  XNOR64 xnor64_1 (.A(A), .Result(xnor64_1_result));  // open: B
  // XOR64 xor64_1: pin names not known; wires that end beside it: B, A, xor64_1_p3
  Clear64 clear64_1 (.Result({Negative, clear64_1_result}));
  Multiplexer #(.select(4), .width(64)) multiplexer_1 (
    .in0(adder64_1_result), .in1(incrementer64_1_result), .in2(decrementer64_1_result), .in4(not64_1_result),
    .in5(and64_1_result), .in6(or64_1_result), .in7(leftshift64_1_result), .in8(rightshift64_1_result),
    .in9(nand64_1_result), .in10(nor64_1_result), .in11(xnor64_1_result), .in12(xor64_1_p3),
    .in13({Negative, clear64_1_result}), .out(ALUResult), .sel(OpCodeIn));  // open: in3, in14, in15
  assign OR_out = clear64_1_result | Negative;  // OR_Gate OR, 32 bits wide
  assign ZERO = ~OR_out;  // NOT_Gate not_1, 32 bits wide
endmodule

// CU
module CU64 (
  input  [3:0] Instruction,
  input  ClkIn,
  output [3:0] OpCodeOut
);

  Register #(.width(4)) InstructionReg (.D(Instruction), .clk(ClkIn), .Q(OpCodeOut));  // open: en, clr
endmodule

// NOT
module NOT64 (
  input  [63:0] A,
  output [63:0] Result
);

  assign Result = ~A;  // NOT_Gate not_1, 64 bits wide
endmodule

// NAND
module NAND64 (
  input  [63:0] A,
  input  [63:0] B,
  output [63:0] Result
);

  assign Result = ~(A & B);  // NAND_Gate nand_1, 64 bits wide
endmodule

// NOR
module NOR64 (
  input  [63:0] A,
  input  [63:0] B,
  output [63:0] Result
);

  assign Result = ~(A | B);  // NOR_Gate nor_1, 64 bits wide
endmodule

// XNOR
module XNOR64 (
  input  [63:0] A,
  input  [63:0] B,
  output [63:0] Result
);

  assign Result = ~(A ^ B);  // XNOR_Gate xnor_1, 64 bits wide
endmodule

// INCR
module Incrementer64 (
  input  [63:0] Control,
  input  [63:0] A,
  output [63:0] Result,
  output [63:0] CarryOut,
  output [63:0] Overflow
);

  wire [63:0] and_1_out, AND_2_out, not_1_out, not_2_out, not_3_out;

  assign not_1_out = ~64'h1;  // NOT_Gate not_1, 64 bits wide
  assign not_2_out = ~A;  // NOT_Gate not_2, 64 bits wide
  FullAdder64 fulladder64_1 (.A(A), .B(64'h1), .In(Control), .Out(CarryOut), .Result(Result));
  assign and_1_out = Result & not_2_out & not_1_out;  // AND_Gate and_1, 64 bits wide
  assign not_3_out = ~Result;  // NOT_Gate not_3, 64 bits wide
  assign AND_2_out = not_3_out & A & 64'h1;  // AND_Gate AND_2, 64 bits wide
  assign Overflow = and_1_out | AND_2_out;  // OR_Gate or_1, 64 bits wide
endmodule

// DECR
module Decrementer64 (
  input  [63:0] Control,
  input  [63:0] A,
  output [63:0] Result,
  output [63:0] CarryOut,
  output [63:0] Overflow
);

  wire [63:0] and_1_out, AND_2_out, not_1_out, not_2_out, not_3_out;

  assign not_1_out = ~{64{1'b1}};  // NOT_Gate not_1, 64 bits wide
  assign not_2_out = ~A;  // NOT_Gate not_2, 64 bits wide
  FullAdder64 fulladder64_1 (.A(A), .B({64{1'b1}}), .In(Control), .Out(CarryOut), .Result(Result));
  assign and_1_out = Result & not_2_out & not_1_out;  // AND_Gate and_1, 64 bits wide
  assign not_3_out = ~Result;  // NOT_Gate not_3, 64 bits wide
  assign AND_2_out = not_3_out & A & {64{1'b1}};  // AND_Gate AND_2, 64 bits wide
  assign Overflow = and_1_out | AND_2_out;  // OR_Gate or_1, 64 bits wide
endmodule

// COMP
module Comparator64 (
  input  [63:0] A,
  input  [63:0] B,
  output GT,
  output EQ,
  output LT
);

  Comparator #(.width(64)) comparator_1 (.a(A), .b(B), .gt(GT), .eq(EQ), .lt(LT));
endmodule

// LSHFT
module LeftShift64 (
  input  [63:0] A,
  output [63:0] Result
);

  Shifter #(.width(64)) shifter_1 (.in(A), .\dist (6'b000001), .out(Result));
endmodule

// RSHFT
module RightShift64 (
  input  [63:0] A,
  output [63:0] Result
);

  Shifter #(.shift("lr"), .width(64)) shifter_1 (.in(A), .\dist (6'b000001), .out(Result));
endmodule

// XOR
module XOR64 (
  input  [63:0] A,
  input  [63:0] B,
  output [63:0] Result
);

  assign Result = A ^ B;  // XOR_Gate xor_1, 64 bits wide
endmodule

// CLR
module Clear64 (
  output [63:0] Result
);


  assign Result = {64{1'b0}};
endmodule

module CPU64Bit (
  input  [3:0] Instruction,
  input  [63:0] B,
  input  [63:0] A,
  output [63:0] Overflow,
  output LT,
  output EQ,
  output GT,
  output [63:0] ALUResult,
  output [31:0] ZERO,
  output [63:0] Carryout,
  output [31:0] Negative
);

  wire clock_1_out;
  wire [3:0] cu64_1_opcodeout;

  Clock clock_1 (.out(clock_1_out));
  CU64 cu64_1 (.ClkIn(clock_1_out), .Instruction(Instruction), .OpCodeOut(cu64_1_opcodeout));
  ALU64 alu64_1 (
    .Carryout(Carryout), .A(A), .GT(GT), .EQ(EQ), .LT(LT), .Overflow(Overflow), .OpCodeIn(cu64_1_opcodeout),
    .B(B), .ALUResult(ALUResult), .ZERO(ZERO), .Negative(Negative));
endmodule
